# Fritzing sketch D1mini_Strip_Temp (saved by Fritzing 0.9.3b)
stripboards: 1

parts:
  J5 = JST-B3P-VH [part_number=WS2812 package=THT]
  J4 = JST-B3P-VH [part_number=DS18D20 package=THT]
  R4 = Resistor [tolerance=±5% resistance=470 package=THT]
  WeMos_D1_Mini1 = WeMos D1 Mini
  R6 = Resistor [tolerance=±5% resistance=4.7k package=THT]
  VCC1_5V = 4 x AAA Battery Mount

nets:
  N1: J5.pin2, R4.Pin_1
  N2: J5.pin1, J4.pin1, WeMos_D1_Mini1.G, VCC1_5V.-
  N3: J5.pin3, WeMos_D1_Mini1.5V, VCC1_5V.+
  N4: J4.pin2, WeMos_D1_Mini1.D5, R6.Pin_1
  N5: J4.pin3, WeMos_D1_Mini1.3V3, R6.Pin_0
  N6: R4.Pin_0, WeMos_D1_Mini1.D3
